# Fritzing sketch portcullis-top (saved by Fritzing 1.0.3b)
circuit board: 2.99999cm x 12.9cm
breadboards: 2

parts:
  Att = Rotary Potentiometer (Small) [maximum_resistance=100kΩ knob_status=50% power=0.5W package=THT]
  Rel = Rotary Potentiometer (Small) [maximum_resistance=0.1MΩ knob_status=50% power=0.5W package=THT]
  IN1 = PJ-301M [part_number=PJ-301M]  # not connected
  Out1 = PJ-301M [part_number=PJ-301M]  # not connected
  CV1 = PJ-301M [part_number=PJ-301M]  # not connected
  G1 = PJ-301M [part_number=PJ-301M]  # not connected
  Out2 = PJ-301M [part_number=PJ-301M]  # not connected
  IN2 = PJ-301M [part_number=PJ-301M]  # not connected
  G2 = PJ-301M [part_number=PJ-301M]  # not connected
  Rel_2 = Rotary Potentiometer (Small) [maximum_resistance=100kΩ knob_status=50% power=0.5W package=THT]
  Att_2 = Rotary Potentiometer (Small) [maximum_resistance=100kΩ knob_status=50% power=0.5W package=THT]
  CV2 = PJ-301M [part_number=PJ-301M]  # not connected

nets:
  N1: Att.wiper, Att.leg2
  N2: Rel.wiper, Rel.leg2
  N3: Rel_2.wiper, Rel_2.leg2
  N4: Att_2.wiper, Att_2.leg2

notes:
  blueprint@poetaster . de 2025
  jlcjlcjlcjlcjlc
  jlcjlcjlcjlc
  poetaster's
  tonetoys
  ext
  gate
  out
  attack
  portcullis
  in
  release

custom parts:
  PJ-301M: Phone power jack.
