# Fritzing sketch portcullis (saved by Fritzing 1.0.4)
circuit board: 2.99999cm x 11cm
breadboards: 2

parts:
  REL = Rotary Potentiometer (Small) [maximum_resistance=1MΩ knob_status=50% power=0.5W package=THT]
  ATT = Rotary Potentiometer (Small) [maximum_resistance=1MΩ knob_status=50% power=0.5W package=THT]
  100K = Resistor [tolerance=±5% resistance=100k power=0.25W package=THT]
  IN1 = PJ-301M [part_number=PJ-301M]
  103 = Ceramic Capacitor [capacitance=10nF voltage=16V package="200 mil [THT, multilayer]"]
  104 = Ceramic Capacitor [capacitance=100nF voltage=16V package="200 mil [THT, multilayer]"]
  J3 = shrouded pin header, 16 pins [form="♂ (shrouded male)"]
  4001 = Diode [package=diode-1n4148]
  Out1 = PJ-301M [part_number=PJ-301M]
  CV1 = PJ-301M [part_number=PJ-301M]
  G1 = PJ-301M [part_number=PJ-301M]
  Out2 = PJ-301M [part_number=PJ-301M]
  IN2 = PJ-301M [part_number=PJ-301M]
  G2 = PJ-301M [part_number=PJ-301M]
  TL074 = TL074 Quad Opamp (Movable) [package="DIP (Dual Inline)"]
  TL074_PWR = TL074 Quad Opamp (Movable) [package="DIP (Dual Inline)"]
  TL074_A = TL074 Quad Opamp (Movable) [package="DIP (Dual Inline)"]
  TL074_B = TL074 Quad Opamp (Movable) [package="DIP (Dual Inline)"]
  TL074_C = TL074 Quad Opamp (Movable) [package="DIP (Dual Inline)"]
  TL074_D = TL074 Quad Opamp (Movable) [package="DIP (Dual Inline)"]
  ATT_2 = Rotary Potentiometer (Small) [maximum_resistance=1MΩ knob_status=50% power=0.5W package=THT]
  REL_2 = Rotary Potentiometer (Small) [maximum_resistance=1MΩ knob_status=50% power=0.5W package=THT]
  Vactrol1 = VTL5C1
  CV2 = PJ-301M [part_number=PJ-301M]
  Vactrol2 = VTL5C1
  J4 = female pin header, 1 pin [form="♀ (female)"]
  100uF = Electrolytic Capacitor [capacitance=0.1mF voltage=35V package="100 mil [THT, electrolytic]"]
  4_7k = Resistor [tolerance=±5% power=0.25W resistance=4.7k package=THT]
  106 = Ceramic Capacitor [capacitance=10µF voltage=16V package="200 mil [THT, multilayer]"]
  4148 = Diode [package=diode-1n4148]
  4148_2 = Diode [package=diode-1n4148]
  4148_3 = Diode [package=diode-1n4148]
  4148_4 = Diode [package=diode-1n4148]
  4148_5 = Diode [package=diode-1n4148]
  4148_6 = Diode [package=diode-1n4148]
  100K_2 = Resistor [tolerance=±5% resistance=100k power=0.25W package=THT]
  106_2 = Ceramic Capacitor [capacitance=10µF voltage=16V package="200 mil [THT, multilayer]"]
  4_7k_2 = Resistor [tolerance=±5% power=0.25W resistance=4.7k package=THT]
  4148_7 = Diode [package=diode-1n4148]
  4148_8 = Diode [package=diode-1n4148]
  1uF = Electrolytic Capacitor [capacitance=1µF voltage=35V package="100 mil [THT, electrolytic]"]
  1uF1 = Electrolytic Capacitor [capacitance=1µF voltage=35V package="100 mil [THT, electrolytic]"]

nets:
  N1: REL.leg1, 4148_2.A
  N2: REL.wiper, REL.leg2, ATT.wiper, ATT.leg2, TL074.connector9, TL074_C.3IN+, 106.1
  N3: ATT.leg1, 4148_3.C
  N4: 100K.Pin_0, TL074.connector11, TL074_D.4IN+, 4148.C
  GND: 100K.Pin_1, IN1.Pin_1, 103.0, 104.1, J3.pin2, J3.pin3, J3.pin4, J3.pin13, J3.pin14, J3.pin15, Out1.Pin_1, CV1.Pin_1, G1.Pin_1, Out2.Pin_1, IN2.Pin_1, G2.Pin_1, TL074.connector10, TL074_PWR.VCC-, CV2.Pin_1, 100uF.-, 4_7k.Pin_1, 106.0, 100K_2.Pin_0, 106_2.1, 4_7k_2.Pin_1, 1uF.-, 1uF1.-
  N5: IN1.Pin_2, CV1.Pin_2, 4148_4.C
  N6: IN1.Pin_3, Vactrol1.Pin_4
  N7: 103.1, 104.0, 4001.C, TL074.connector3, TL074_PWR.VCC+, J4.pin1, 100uF.+
  N8: J3.pin1, J3.pin16
  9V: J3.pin5, J3.pin6, J3.pin11, J3.pin12, 4001.A
  N9: J3.pin7, J3.pin10
  N10: J3.pin8, J3.pin9
  N11: Out1.Pin_3, Vactrol1.Pin_3, 1uF.+
  N12: CV1.Pin_3, Vactrol1.Pin_2
  N13: G1.Pin_3, 4148.A
  N14: Out2.Pin_3, Vactrol2.Pin_4, 1uF1.+
  N15: IN2.Pin_2, CV2.Pin_2, 4148_7.C
  N16: IN2.Pin_3, Vactrol2.Pin_3
  N17: G2.Pin_3, 4148_8.A
  N18: TL074.connector0, TL074.connector1, TL074_A.1OUT, TL074_A.1IN-, 4148_5.C, 4148_6.A
  N19: TL074.connector2, TL074_A.1IN+, 100K_2.Pin_1, 4148_8.C
  N20: TL074.connector4, TL074_B.2IN+, ATT_2.wiper, ATT_2.leg2, REL_2.wiper, REL_2.leg2, 106_2.0
  N21: TL074.connector5, TL074.connector6, TL074_B.2IN-, TL074_B.2OUT, 4148_7.A
  N22: TL074.connector7, TL074.connector8, TL074_C.3OUT, TL074_C.3IN-, 4148_4.A
  N23: TL074.connector12, TL074.connector13, TL074_D.4IN-, TL074_D.4OUT, 4148_2.C, 4148_3.A
  N24: ATT_2.leg1, 4148_6.C
  N25: REL_2.leg1, 4148_5.A
  N26: Vactrol1.Pin_1, 4_7k.Pin_0
  N27: CV2.Pin_3, Vactrol2.Pin_2
  N28: Vactrol2.Pin_1, 4_7k_2.Pin_0

notes:
  portcullis
  blueprint@poetaster . de 2025
  jlcjlcjlcjlcjlc

custom parts:
  PJ-301M: Phone power jack.
  TL074 Quad Opamp (Movable): Quadruple Operational Amplifier (Opamp)
  TL074 Quad Opamp (Movable): Quadruple Operational Amplifier (Opamp)
  TL074 Quad Opamp (Movable): Quadruple Operational Amplifier (Opamp)
  TL074 Quad Opamp (Movable): Quadruple Operational Amplifier (Opamp)
  TL074 Quad Opamp (Movable): Quadruple Operational Amplifier (Opamp)
  TL074 Quad Opamp (Movable): Quadruple Operational Amplifier (Opamp)
  VTL5C1: Xvive5C1-R OPTO-ISOLATOR SPECICATION.
